// Logisim project TinyCPU-FetchDecode.circ as structural Verilog: 1 circuit, main circuit FetchDecode
module FetchDecode (
  input  CLK,
  input  RESET,
  input  ZERO,
  input  [15:0] PROGRAM_LIMIT,
  input  NEGATIVE,
  input  ERROR,
  output [15:0] OPERAND,
  output [15:0] PC_OUT,
  output LOAD_CONST,
  output LOAD_ADDRESS,
  output LOAD_ADDRESS_REGISTER,
  output LOAD_ADDRESS_REGISTER_PLUS_OFFSET,
  output ADD_CONST,
  output ADD_ADDRESS,
  output ADD_ADDRESS_REGISTER,
  output ADD_ADDRESS_REGISTER_PLUS_OFFSET,
  output SUB_CONST,
  output SUB_ADDRESS,
  output SUB_ADDRESS_REGISTER,
  output SUB_ADDRESS_REGISTER_PLUS_OFFSET,
  output MUL_CONST,
  output MUL_ADDRESS,
  output MUL_ADDRESS_REGISTER,
  output MUL_ADDRESS_REGISTER_PLUS_OFFSET,
  output DIV_CONST,
  output DIV_ADDRESS,
  output DIV_ADDRESS_REGISTER,
  output DIV_ADDRESS_REGISTER_PLUS_OFFSET,
  output AND_CONST,
  output AND_ADDRESS,
  output AND_ADDRESS_REGISTER,
  output AND_ADDRESS_REGISTER_PLUS_OFFSET,
  output OR_CONST,
  output OR_ADDRESS,
  output OR_ADDRESS_REGISTER,
  output OR_ADDRESS_REGISTER_PLUS_OFFSET,
  output STORE_ADDRESS,
  output STORE_ADDRESS_REGISTER,
  output STORE_ADDRESS_REGISTER_PLUS_OFFSET,
  output LOAD_ADDRESS_REGISTER_CONST,
  output LOAD_ADDRESS_REGISTER_ADDRESS,
  output NOT,
  output JUMP_ADDRESS,
  output JUMP_ZERO,
  output JUMP_NOT_ZERO,
  output JUMP_NEGATIVE,
  output JUMP_ERROR,
  output JUMP_NOT_ERROR,
  output CLEAR_ERROR,
  output INPUT,
  output PRINT,
  output PRINT_ADDRESS,
  output HALT,
  output HALT_ERROR,
  output SET_OVF,
  output SET_DIV0,
  output SET_ADDR,
  output SET_INV,
  output SET_ILL,
  output SET_INPUT
);

  wire ISA_DECODER_p1;
  wire [15:0] PC_INCREMENT_p3;

  Register #(.width(16)) PC (
    .D(PC_INCREMENT_p3), .clk(CLK), .Q({PC_OUT[15:4], PC_OUT[15:12]}), .clr(RESET));  // open: en
  // Adder #(.width(16)) PC_INCREMENT: pin names not known; wires that end beside it: NEGATIVE, {PC_OUT[15:4], PC_OUT[15:12]}, PC_INCREMENT_p3
  Multiplexer #(.width(16)) PC_SOURCE (.out(PC_INCREMENT_p3));  // open: in0, in1, sel
  ROM #(.addrWidth(12), .dataWidth(22)) INSTRUCTION_ROM (.addr({PC_OUT[11:4], PC_OUT[15:12]}));  // open: data
  // Comparator #(.width(16)) PC_RANGE: pin names not known; wires that end beside it: {PC_OUT[15:4], PC_OUT[15:12]}, PROGRAM_LIMIT
  // Decoder #(.select(6)) ISA_DECODER: pin names not known; wires that end beside it: ISA_DECODER_p1
  // AND_Gate JNZ_TAKEN has open pins: out=ZERO
  // OR_Gate ERROR_HALT has open pins: out=ERROR
  // Pins of 4 and 12 bits meet at {PC_OUT[11:4], PC_OUT[15:12]}
  // Pins of 6 and 16 bits meet at OPERAND

  assign PC_OUT[3:0] = PC_OUT[15:12];

  // Other names for the same wires on the sheet: SET_INPUT_DECODE = SET_INPUT

  // Notes on the sheet:
  //   AP 7 machine format v1: stable six-bit opcode allocation and encoder-generated ROM
  //   contents of INSTRUCTION_ROM (hex, n*v repeats v):
  //   00ffff 1c0065 000003 1c0064 2a0000 050065 1c0064 240004 2c0000
endmodule
